// Logisim project ALU.circ as structural Verilog: 3 circuits, main circuit Arithmetic_unit
module Arithmetic_unit (
  input  [1:0] op,
  input  [15:0] Y,
  input  [15:0] X,
  output [15:0] out_4
);

  wire [15:0] adder_1_out, adder_2_out, subtractor_1_out, subtractor_2_out;

  Adder #(.width(16)) adder_1 (.a(Y), .b(X), .out(adder_1_out));  // open: cin, cout
  Adder #(.width(16)) adder_2 (.a(X), .b(Y), .out(adder_2_out));  // open: cin, cout
  Subtractor #(.width(16)) subtractor_1 (.a(X), .b(16'h1), .out(subtractor_1_out));  // open: bin, bout
  Subtractor #(.width(16)) subtractor_2 (.a(X), .b(16'h1), .out(subtractor_2_out));  // open: bin, bout
  Multiplexer #(.select(2), .width(16)) multiplexer_1 (
    .in0(adder_1_out), .in1(adder_2_out), .in2(subtractor_1_out), .in3(subtractor_2_out), .out(out_4),
    .sel(op));
endmodule

module Logic_unit (
  input  [1:0] op,
  input  [15:0] Y,
  input  [15:0] X,
  output [15:0] out_4
);

  wire [15:0] and_1_out, not_1_out, or_1_out, xor_1_out;

  assign and_1_out = Y & X;  // AND_Gate and_1, 16 bits wide
  assign or_1_out = Y | X;  // OR_Gate or_1, 16 bits wide
  assign xor_1_out = Y ^ X;  // XOR_Gate xor_1, 16 bits wide
  assign not_1_out = ~X;  // NOT_Gate not_1, 16 bits wide
  Multiplexer #(.select(2), .width(16)) multiplexer_1 (
    .in0(and_1_out), .in1(or_1_out), .in2(xor_1_out), .in3(not_1_out), .out(out_4), .sel(op));
endmodule

module ALU (
  input  [2:0] u_op,
  input  [15:0] Y,
  input  [15:0] X,
  input  sw,
  input  zx,
  output [15:0] out_6
);

  wire [15:0] arithmetic_unit_1_out_4, logic_unit_1_out_4, multiplexer_1_out, multiplexer_2_out,
       multiplexer_3_out;

  Multiplexer #(.width(16)) multiplexer_1 (.in0(Y), .in1(X), .out(multiplexer_1_out), .sel(sw));
  Multiplexer #(.width(16)) multiplexer_2 (.in0(X), .in1(Y), .out(multiplexer_2_out), .sel(sw));
  Multiplexer #(.width(16)) multiplexer_3 (
    .in0(multiplexer_2_out), .in1({16{1'b0}}), .out(multiplexer_3_out), .sel(zx));
  Logic_unit logic_unit_1 (.op(u_op[1:0]), .Y(multiplexer_1_out), .X(multiplexer_3_out), .out_4(logic_unit_1_out_4));
  Arithmetic_unit arithmetic_unit_1 (
    .op(u_op[1:0]), .Y(multiplexer_1_out), .X(multiplexer_3_out), .out_4(arithmetic_unit_1_out_4));
  Multiplexer #(.width(16)) multiplexer_4 (
    .in0(logic_unit_1_out_4), .in1(arithmetic_unit_1_out_4), .out(out_6), .sel(u_op[2]));

  // Notes on the sheet:
  //   Y'
  //   X'
endmodule
