// Logisim project Combined_memory.circ as structural Verilog: 1 circuit, main circuit Combined_memory
module Combined_memory (
  input  clk,
  input  w_a,
  input  w_d,
  input  w_m,
  input  [15:0] X,
  output [15:0] A,
  output [15:0] D,
  output [15:0] MEM
);

  Register #(.width(16)) reg_A (.D(X), .en(w_a), .clk(clk), .Q(A));  // open: clr
  Register #(.width(16)) reg_D (.D(X), .en(w_d), .clk(clk), .Q(D));  // open: clr
  RAM #(.addrWidth(16), .dataWidth(16)) ram_1 (.addr(A), .we(w_m), .oe(1'b1), .clk(clk), .din(X), .dout(MEM));
endmodule
