// Logisim project Condition.circ as structural Verilog: 1 circuit, main circuit Condition
module Condition (
  input  gt,
  input  eq,
  input  [15:0] X,
  input  lt,
  output out_5
);

  wire comparator_1_eq, comparator_1_gt, comparator_1_lt, multiplexer_1_out, multiplexer_2_out,
       multiplexer_3_out;

  Comparator #(.width(16)) comparator_1 (
    .a(X), .b({16{1'b0}}), .gt(comparator_1_gt), .eq(comparator_1_eq), .lt(comparator_1_lt));
  Multiplexer multiplexer_1 (.in0(1'b0), .in1(comparator_1_gt), .out(multiplexer_1_out), .sel(gt));
  Multiplexer multiplexer_2 (.in0(1'b0), .in1(comparator_1_eq), .out(multiplexer_2_out), .sel(eq));
  Multiplexer multiplexer_3 (.in0(1'b0), .in1(comparator_1_lt), .out(multiplexer_3_out), .sel(lt));
  or or_1 (out_5, multiplexer_1_out, multiplexer_2_out, multiplexer_3_out);
endmodule
