// Logisim project Processing_unit.circ as structural Verilog: 1 circuit, main circuit main
module main (
  input  [15:0] I,
  input  [15:0] A,
  input  [15:0] D,
  input  [15:0] MEM,
  output add_mem,
  output reg_d,
  output reg_a,
  output [15:0] R,
  output j
);

  wire [15:0] multiplexer_1_out;

  Multiplexer #(.width(16)) multiplexer_1 (.in0(A), .in1(MEM), .out(multiplexer_1_out), .sel(I[12]));
  ALU alu_1 (.u_op(I[10:8]), .Y(multiplexer_1_out), .X(D), .sw(I[6]), .zx(I[7]), .out_6(R));
  Condition condition_1 (.gt(I[0]), .eq(I[1]), .X(R), .lt(I[2]), .out_5(j));

  assign add_mem = I[3];
  assign reg_a = I[5];
  assign reg_d = I[4];
endmodule
