// Logisim project microprocessor.circ as structural Verilog: 9 circuits, main circuit CPU
module CPU (
  input  clk,
  input  clk_select,
  input  reset,
  input  start_instr,
  input  clk_enable
);

  wire clock_1_out, cu_1_j, cu_1_w_a, cu_1_w_d, cu_1_w_mem, multiplexer_1_out;
  wire [15:0] combined_memory_1_a, combined_memory_1_d, combined_memory_1_mem, counter_1_q, cu_1_r,
       multiplexer_2_out, PROM_data;

  Clock clock_1 (.out(clock_1_out));
  Multiplexer multiplexer_1 (.in0(clock_1_out), .in1(clk), .out(multiplexer_1_out), .sel(clk_select));
  Multiplexer #(.width(16)) multiplexer_2 (
    .in0(counter_1_q), .in1(combined_memory_1_a), .out(multiplexer_2_out), .sel(cu_1_j));
  Counter #(.max('hffff), .width(16)) counter_1 (
    .clr(reset), .load(start_instr), .up(1'b1), .count(clk_enable), .clk(multiplexer_1_out),
    .D(multiplexer_2_out), .Q(counter_1_q));  // open: carry
  ROM #(.addrWidth(16), .dataWidth(16)) PROM (.addr(counter_1_q), .data(PROM_data));
  CU cu_1 (
    .I(PROM_data), .A(combined_memory_1_a), .D(combined_memory_1_d), .MEM(combined_memory_1_mem), .R(cu_1_r),
    .w_a(cu_1_w_a), .w_d(cu_1_w_d), .w_mem(cu_1_w_mem), .j(cu_1_j));
  Combined_memory combined_memory_1 (
    .clk(multiplexer_1_out), .w_a(cu_1_w_a), .w_d(cu_1_w_d), .w_mem(cu_1_w_mem), .X(cu_1_r),
    .A(combined_memory_1_a), .D(combined_memory_1_d), .MEM(combined_memory_1_mem));

  // Notes on the sheet:
  //   contents of PROM (hex, n*v repeats v):
  //   80a0 8090 c 8490 8510 8410 8510 8128 8018 8322 8610 8710
endmodule

module Combined_memory (
  input  clk,
  input  w_a,
  input  w_d,
  input  w_mem,
  input  [15:0] X,
  output [15:0] A,
  output [15:0] D,
  output [15:0] MEM
);

  Register #(.width(16)) reg_A (.D(X), .en(w_a), .clk(clk), .Q(A));  // open: clr
  Register #(.width(16)) reg_D (.D(X), .en(w_d), .clk(clk), .Q(D));  // open: clr
  RAM #(.addrWidth(16), .dataWidth(16)) ram_1 (.addr(A), .we(w_mem), .oe(1'b1), .clk(clk), .din(X), .dout(MEM));
endmodule

module replace_condition (
  input  gt,
  input  [15:0] X,
  input  eq,
  input  lt,
  output out_5
);

  wire comparator_1_eq, comparator_1_gt, comparator_1_lt, multiplexer_1_out, multiplexer_2_out,
       multiplexer_3_out;

  Comparator #(.width(16)) comparator_1 (
    .a(X), .b({16{1'b0}}), .gt(comparator_1_gt), .eq(comparator_1_eq), .lt(comparator_1_lt));
  Multiplexer multiplexer_1 (.in0(1'b0), .in1(comparator_1_gt), .out(multiplexer_1_out), .sel(gt));
  Multiplexer multiplexer_2 (.in0(1'b0), .in1(comparator_1_eq), .out(multiplexer_2_out), .sel(eq));
  Multiplexer multiplexer_3 (.in0(1'b0), .in1(comparator_1_lt), .out(multiplexer_3_out), .sel(lt));
  or or_1 (out_5, multiplexer_1_out, multiplexer_2_out, multiplexer_3_out);
endmodule

module Logic_unit (
  input  [1:0] op,
  input  [15:0] Y,
  input  [15:0] X,
  output [15:0] out_4
);

  wire [15:0] and_1_out, not_1_out, or_1_out, xor_1_out;

  assign and_1_out = Y & X;  // AND_Gate and_1, 16 bits wide
  assign or_1_out = Y | X;  // OR_Gate or_1, 16 bits wide
  assign xor_1_out = Y ^ X;  // XOR_Gate xor_1, 16 bits wide
  assign not_1_out = ~X;  // NOT_Gate not_1, 16 bits wide
  Multiplexer #(.select(2), .width(16)) multiplexer_1 (
    .in0(and_1_out), .in1(or_1_out), .in2(xor_1_out), .in3(not_1_out), .out(out_4), .sel(op));
endmodule

module Arithmetic_unit (
  input  [1:0] op,
  input  [15:0] Y,
  input  [15:0] X,
  output [15:0] out_4
);

  wire [15:0] adder_1_out, adder_2_out, subtractor_1_out, subtractor_2_out;

  Adder #(.width(16)) adder_1 (.a(Y), .b(X), .out(adder_1_out));  // open: cin, cout
  Adder #(.width(16)) adder_2 (.a(X), .b(16'h1), .out(adder_2_out));  // open: cin, cout
  Subtractor #(.width(16)) subtractor_1 (.a(X), .b(Y), .out(subtractor_1_out));  // open: bin, bout
  Subtractor #(.width(16)) subtractor_2 (.a(X), .b(16'h1), .out(subtractor_2_out));  // open: bin, bout
  Multiplexer #(.select(2), .width(16)) multiplexer_1 (
    .in0(adder_1_out), .in1(adder_2_out), .in2(subtractor_1_out), .in3(subtractor_2_out), .out(out_4),
    .sel(op));

  // Notes on the sheet:
  //   u=1 -> arithmetic
  //   op : 00 X+Y
  //   op : 01 X+1
  //   op : 10 X-Y
  //   op : 11 X-1
endmodule

module PU (
  input  [15:0] I,
  input  [15:0] A,
  input  [15:0] D,
  input  [15:0] MEM,
  output w_mem,
  output w_d,
  output w_a,
  output [15:0] R,
  output j
);

  wire [15:0] multiplexer_1_out;

  Multiplexer #(.width(16)) multiplexer_1 (.in0(A), .in1(MEM), .out(multiplexer_1_out), .sel(I[12]));
  ALU alu_1 (.u_op(I[10:8]), .A(multiplexer_1_out), .D(D), .sw(I[6]), .zx(I[7]), .out_6(R));
  Condition condition_1 (.gt(I[0]), .X(R), .eq(I[1]), .lt(I[2]), .out_5(j));

  assign w_a = I[5];
  assign w_d = I[4];
  assign w_mem = I[3];

  // Notes on the sheet:
  //   15..8 :
  //   7..0 :
  //   t - x - x - mem_in - x - u - op1 - op0
  //   zx - sw - w_a - w_d - w_mem - lt - eq - gt
  //   RAM output
endmodule

module CU (
  input  [15:0] I,
  input  [15:0] A,
  input  [15:0] D,
  input  [15:0] MEM,
  output [15:0] R,
  output w_a,
  output w_d,
  output w_mem,
  output j
);

  wire not_1_out, pu_1_j, pu_1_w_a, pu_1_w_d, pu_1_w_mem;
  wire [15:0] pu_1_r;

  PU pu_1 (.I(I), .A(A), .D(D), .MEM(MEM), .w_mem(pu_1_w_mem), .w_d(pu_1_w_d), .w_a(pu_1_w_a), .R(pu_1_r), .j(pu_1_j));
  Multiplexer #(.width(16)) multiplexer_1 (.in0(I), .in1(pu_1_r), .out(R), .sel(I[15]));
  not not_1 (not_1_out, I[15]);
  and and_1 (w_d, I[15], pu_1_w_d);
  and and_2 (w_mem, I[15], pu_1_w_mem);
  and and_3 (j, I[15], pu_1_j);
  or or_1 (w_a, not_1_out, pu_1_w_a);
endmodule

module ALU (
  input  [2:0] u_op,
  input  [15:0] A,
  input  [15:0] D,
  input  sw,
  input  zx,
  output [15:0] out_6
);

  wire [15:0] arithmetic_unit_1_out_4, logic_unit_1_out_4, multiplexer_1_out, multiplexer_2_out,
       multiplexer_3_out;

  Multiplexer #(.width(16)) multiplexer_1 (.in0(A), .in1(D), .out(multiplexer_1_out), .sel(sw));
  Multiplexer #(.width(16)) multiplexer_2 (.in0(D), .in1(A), .out(multiplexer_2_out), .sel(sw));
  Multiplexer #(.width(16)) multiplexer_3 (
    .in0(multiplexer_2_out), .in1({16{1'b0}}), .out(multiplexer_3_out), .sel(zx));
  Logic_unit logic_unit_1 (.op(u_op[1:0]), .Y(multiplexer_1_out), .X(multiplexer_3_out), .out_4(logic_unit_1_out_4));
  Arithmetic_unit arithmetic_unit_1 (
    .op(u_op[1:0]), .Y(multiplexer_1_out), .X(multiplexer_3_out), .out_4(arithmetic_unit_1_out_4));
  Multiplexer #(.width(16)) multiplexer_4 (
    .in0(logic_unit_1_out_4), .in1(arithmetic_unit_1_out_4), .out(out_6), .sel(u_op[2]));

  // Notes on the sheet:
  //   sw=1 -> Y'=X , X' = Y
  //   u=0 -> logic
  //   op : 00 and
  //   op : 01 or
  //   op : 10 xor
  //   op : 11 not X
  //   Y
  //   X
  //   zx=1 -> X'=0
  //   u=1 -> arithmetic
  //   op : 00 X+Y
  //   op : 01 X+1
  //   op : 10 X-Y
  //   op : 11 X-1
endmodule

module Condition (
  input  gt,
  input  [15:0] X,
  input  eq,
  input  lt,
  output out_5
);

  wire comparator_1_eq, comparator_1_gt, comparator_1_lt, multiplexer_1_out, multiplexer_2_out,
       multiplexer_3_out;

  Comparator #(.width(16)) comparator_1 (
    .a(X), .b({16{1'b0}}), .gt(comparator_1_gt), .eq(comparator_1_eq), .lt(comparator_1_lt));
  Multiplexer multiplexer_1 (.in0(1'b0), .in1(comparator_1_gt), .out(multiplexer_1_out), .sel(gt));
  Multiplexer multiplexer_2 (.in0(1'b0), .in1(comparator_1_eq), .out(multiplexer_2_out), .sel(eq));
  Multiplexer multiplexer_3 (.in0(1'b0), .in1(comparator_1_lt), .out(multiplexer_3_out), .sel(lt));
  or or_1 (out_5, multiplexer_1_out, multiplexer_2_out, multiplexer_3_out);
endmodule
