// Logisim project microprocessor.circ as structural Verilog: 5 circuits, main circuit CPU
module CPU (
  input  reset,
  input  enable
);

  wire and_1_out, clock_1_out, Control_unit_cmp, Control_unit_i1, Control_unit_i_2, Control_unit_jmp,
       Control_unit_load_a, Control_unit_mem_od, Control_unit_r_mem, Control_unit_w_mem, nor_1_out, or_1_out,
       Processing_unit_res_cond;
  wire [1:0] Control_unit_dest, Control_unit_src1, Control_unit_src2;
  wire [2:0] Control_unit_jmp_cond;
  wire [3:0] Control_unit_opcode;
  wire [15:0] bit_extender_1_out, bit_extender_2_out, Memory_unit_operand1, Memory_unit_operand2,
       multiplexer_1_out, multiplexer_2_out, multiplexer_3_out, PC_q, Processing_unit_res, PROM_data;

  Clock clock_1 (.out(clock_1_out));
  Counter #(.max('hffff), .width(16)) PC (
    .clr(reset), .load(and_1_out), .up(1'b1), .count(enable), .clk(clock_1_out), .D(Processing_unit_res),
    .Q(PC_q));  // open: carry
  ROM #(.addrWidth(16), .dataWidth(16)) PROM (.addr(PC_q), .data(PROM_data));
  and and_1 (and_1_out, Control_unit_jmp, or_1_out);
  or or_1 (or_1_out, Processing_unit_res_cond, nor_1_out);
  nor nor_1 (nor_1_out, Control_unit_jmp_cond[0], Control_unit_jmp_cond[1], Control_unit_jmp_cond[2]);
  CU Control_unit (
    .instr(PROM_data), .i_2(Control_unit_i_2), .mem_od(Control_unit_mem_od), .src1(Control_unit_src1),
    .src2(Control_unit_src2), .jmp(Control_unit_jmp), .cmp(Control_unit_cmp), .opcode(Control_unit_opcode),
    .w_mem(Control_unit_w_mem), .r_mem(Control_unit_r_mem), .jmp_cond(Control_unit_jmp_cond),
    .i1(Control_unit_i1), .dest(Control_unit_dest), .load_A(Control_unit_load_a));
  Multiplexer #(.width(16)) multiplexer_1 (
    .in0(Processing_unit_res), .in1(PROM_data), .out(multiplexer_1_out), .sel(Control_unit_load_a));
  Memory Memory_unit (
    .mem_od(Control_unit_mem_od), .r_mem(Control_unit_r_mem), .dest(Control_unit_dest), .reset(reset),
    .w_mem(Control_unit_w_mem), .D_in(multiplexer_1_out), .clk(clock_1_out), .src1(Control_unit_src1),
    .src2(Control_unit_src2), .operand1(Memory_unit_operand1), .operand2(Memory_unit_operand2));
  assign bit_extender_1_out = {{14{1'b0}}, Control_unit_src1};  // Bit_Extender bit_extender_1
  assign bit_extender_2_out = {{14{1'b0}}, Control_unit_src2};  // Bit_Extender bit_extender_2
  Multiplexer #(.width(16)) multiplexer_2 (
    .in0(Memory_unit_operand1), .in1(bit_extender_1_out), .out(multiplexer_2_out), .sel(Control_unit_i1));
  Multiplexer #(.width(16)) multiplexer_3 (
    .in0(Memory_unit_operand2), .in1(bit_extender_2_out), .out(multiplexer_3_out), .sel(Control_unit_i_2));
  PU Processing_unit (
    .opcode(Control_unit_opcode), .operand1(multiplexer_2_out), .operand2(multiplexer_3_out),
    .cmp(Control_unit_cmp), .clk(clock_1_out), .cmp_bits(Control_unit_jmp_cond), .res(Processing_unit_res),
    .res_cond(Processing_unit_res_cond));

  // Notes on the sheet:
  //   contents of PROM (hex, n*v repeats v):
  //   f 8201 1 b880 8231 8431 8001
  //   unconditional jump
endmodule

module ALU (
  input  [3:0] opcode,
  input  [15:0] operand1,
  input  [15:0] operand2,
  output [15:0] res
);

  wire [15:0] adder_1_out, and_1_out, multiplier_1_out, not_1_out, or_1_out, shifter_1_out, shifter_2_out,
       shifter_3_out, subtractor_1_out, xor_1_out;

  Adder #(.width(16)) adder_1 (.a(operand1), .b(operand2), .out(adder_1_out));  // open: cin, cout
  Subtractor #(.width(16)) subtractor_1 (.a(operand1), .b(operand2), .out(subtractor_1_out));  // open: bin, bout
  Multiplier #(.mode("twosComplement"), .width(16)) multiplier_1 (
    .a(operand1), .b(operand2), .out(multiplier_1_out));  // open: cin, cout
  assign and_1_out = operand1 & operand2;  // AND_Gate and_1, 16 bits wide
  assign or_1_out = operand1 | operand2;  // OR_Gate or_1, 16 bits wide
  assign xor_1_out = operand1 ^ operand2;  // XOR_Gate xor_1, 16 bits wide
  assign not_1_out = ~operand2;  // NOT_Gate not_1, 16 bits wide
  Shifter #(.width(16)) shifter_1 (.in(operand1), .\dist (operand2[3:0]), .out(shifter_1_out));
  Shifter #(.shift("lr"), .width(16)) shifter_2 (.in(operand1), .\dist (operand2[3:0]), .out(shifter_2_out));
  Shifter #(.shift("ar"), .width(16)) shifter_3 (.in(operand1), .\dist (operand2[3:0]), .out(shifter_3_out));
  Multiplexer #(.select(4), .width(16)) multiplexer_1 (
    .in0(adder_1_out), .in1(subtractor_1_out), .in2(multiplier_1_out), .in3(and_1_out), .in4(or_1_out),
    .in5(xor_1_out), .in6(not_1_out), .in7(shifter_1_out), .in8(shifter_2_out), .in9(shifter_3_out),
    .in10({16{1'b0}}), .in11({16{1'b0}}), .in12({16{1'b0}}), .in13({16{1'b0}}), .in14({16{1'b0}}),
    .in15({16{1'b0}}), .out(res), .sel(opcode));
endmodule

module PU (
  input  [3:0] opcode,
  input  [15:0] operand1,
  input  [15:0] operand2,
  input  cmp,
  input  clk,
  input  [2:0] cmp_bits,
  output [15:0] res,
  output res_cond
);

  wire and_1_out, and_2_out, and_3_out, comparator_1_eq, comparator_1_gt, comparator_1_lt, eq_q, gt_q, lt_q;

  Comparator #(.width(16)) comparator_1 (
    .a(operand1), .b(operand2), .gt(comparator_1_gt), .eq(comparator_1_eq), .lt(comparator_1_lt));
  Register #(.width(1)) lt (.D(comparator_1_lt), .en(cmp), .clk(clk), .Q(lt_q));  // open: clr
  Register #(.width(1)) eq (.D(comparator_1_eq), .en(cmp), .clk(clk), .Q(eq_q));  // open: clr
  ALU alu_1 (.opcode(opcode), .operand1(operand1), .operand2(operand2), .res(res));
  Register #(.width(1)) gt (.D(comparator_1_gt), .en(cmp), .clk(clk), .Q(gt_q));  // open: clr
  and and_1 (and_1_out, gt_q, cmp_bits[0]);
  and and_2 (and_2_out, eq_q, cmp_bits[1]);
  and and_3 (and_3_out, lt_q, cmp_bits[2]);
  or or_1 (res_cond, and_1_out, and_2_out, and_3_out);

  // Notes on the sheet:
  //   j = 0 :
  //   t - j - op3 - op2 - op1 - op0 - mem_w
  //   i : immediate value, stored in src2
  //   dest1 - dest0 - src1_1 - src1_0 - src2_1 - src2_0 - i
  //   t = 1 -> operation
  //   j = 1 (jump)
  //   t - j - gt - eq - lt - x - x
  //   adr1 - adr0 - x - x - x - x - x
  //   t = 0 -> load value in reg A
endmodule

module CU (
  input  [15:0] instr,
  output i_2,
  output mem_od,
  output w_mem,
  output r_mem,
  output i1,
  output [1:0] src1,
  output [1:0] src2,
  output [1:0] dest,
  output [3:0] opcode,
  output load_A,
  output [2:0] jmp_cond,
  output cmp,
  output jmp
);

  Comparator #(.width(4)) comparator_1 (.a(instr[14:11]), .b(4'b1011), .eq(jmp));  // open: gt, lt
  Comparator #(.width(4)) comparator_2 (.a(instr[14:11]), .b(4'b1010), .eq(cmp));  // open: gt, lt
  and and_1 (w_mem, instr[2], instr[15]);
  and and_2 (r_mem, instr[3], instr[15]);
  not not_1 (load_A, instr[15]);
  Multiplexer #(.width(2)) multiplexer_1 (.in0(instr[10:9]), .in1(2'b00), .out(dest), .sel(load_A));

  assign i1 = instr[4];
  assign i_2 = instr[0];
  assign jmp_cond = instr[2:0];
  assign mem_od = instr[1];
  assign opcode = instr[14:11];
  assign src1 = instr[6:5];
  assign src2 = instr[8:7];
endmodule

// C
module Memory (
  input  [1:0] src1,
  input  [15:0] D_in,
  input  mem_od,
  input  r_mem,
  input  w_mem,
  input  [1:0] dest,
  input  reset,
  input  clk,
  input  [1:0] src2,
  output [15:0] operand1,
  output [15:0] operand2
);

  wire and_1_out, and_2_out, and_3_out, and_4_out, decoder_1_out0, decoder_1_out1, decoder_1_out2,
       decoder_1_out3, decoder_2_out0, decoder_2_out1, decoder_2_out2, decoder_2_out3, decoder_3_out0,
       decoder_3_out1, decoder_3_out2, decoder_3_out3, not_1_out, not_2_out, not_3_out;
  wire [1:0] multiplexer_1_out;
  wire [15:0] A_q, B_q, C_q, controlled_buffer_1_out, controlled_buffer_2_out, D_q, ram_1_dout;

  Decoder #(.select(2)) decoder_1 (
    .out0(decoder_1_out0), .out1(decoder_1_out1), .out2(decoder_1_out2), .out3(decoder_1_out3), .sel(dest),
    .en(not_1_out));
  not not_1 (not_1_out, w_mem);
  Register #(.width(16)) A (.D(D_in), .en(decoder_1_out0), .clk(clk), .Q(A_q), .clr(reset));
  Register #(.width(16)) B (.D(D_in), .en(decoder_1_out1), .clk(clk), .Q(B_q), .clr(reset));
  Register #(.width(16)) C (.D(D_in), .en(decoder_1_out2), .clk(clk), .Q(C_q), .clr(reset));
  Register #(.width(16)) D (.D(D_in), .en(decoder_1_out3), .clk(clk), .Q(D_q), .clr(reset));
  Decoder #(.select(2)) decoder_2 (
    .out0(decoder_2_out0), .out1(decoder_2_out1), .out2(decoder_2_out2), .out3(decoder_2_out3), .sel(src1));  // open: en
  assign controlled_buffer_1_out = decoder_2_out3 ? D_q : 16'bz;  // Controlled_Buffer controlled_buffer_1
  assign controlled_buffer_2_out = decoder_3_out3 ? D_q : 16'bz;  // Controlled_Buffer controlled_buffer_2
  assign controlled_buffer_1_out = decoder_2_out0 ? A_q : 16'bz;  // Controlled_Buffer controlled_buffer_3
  assign controlled_buffer_2_out = decoder_3_out0 ? A_q : 16'bz;  // Controlled_Buffer controlled_buffer_4
  assign controlled_buffer_1_out = decoder_2_out1 ? B_q : 16'bz;  // Controlled_Buffer controlled_buffer_5
  assign controlled_buffer_2_out = decoder_3_out1 ? B_q : 16'bz;  // Controlled_Buffer controlled_buffer_6
  assign controlled_buffer_1_out = decoder_2_out2 ? C_q : 16'bz;  // Controlled_Buffer controlled_buffer_7
  assign controlled_buffer_2_out = decoder_3_out2 ? C_q : 16'bz;  // Controlled_Buffer controlled_buffer_8
  Decoder #(.select(2)) decoder_3 (
    .out0(decoder_3_out0), .out1(decoder_3_out1), .out2(decoder_3_out2), .out3(decoder_3_out3),
    .sel(multiplexer_1_out));  // open: en
  Multiplexer #(.width(2)) multiplexer_1 (.in0(src2), .in1(dest), .out(multiplexer_1_out), .sel(w_mem));
  not not_2 (not_2_out, controlled_buffer_2_out[15]);
  and and_1 (and_1_out, not_2_out, w_mem);
  RAM #(.addrWidth(15), .asyncread("true"), .clearpin("true"), .dataWidth(16)) ram_1 (
    .addr(controlled_buffer_2_out[14:0]), .we(and_1_out), .oe(and_2_out), .clk(clk), .din(D_in),
    .dout(ram_1_dout), .clr(reset));
  and and_2 (and_2_out, not_2_out, r_mem);
  not not_3 (not_3_out, mem_od);
  Multiplexer #(.width(16)) multiplexer_2 (
    .in0(controlled_buffer_1_out), .in1(ram_1_dout), .out(operand1), .sel(and_3_out));
  and and_3 (and_3_out, r_mem, not_3_out);
  and and_4 (and_4_out, mem_od, r_mem);
  Multiplexer #(.width(16)) multiplexer_3 (
    .in0(controlled_buffer_2_out), .in1(ram_1_dout), .out(operand2), .sel(and_4_out));

  // Notes on the sheet:
  //   cannot read AND write
  //   there is only one address port
endmodule
